# Fritzing sketch 7LedDisplayUNO (saved by Fritzing 0.9.3b)
circuit board: 8.46667cm x 5.64444cm
breadboards: 1

parts:
  Часть1 = Arduino Uno (Rev3)
  DI1 = 7-Segment LED Display [package=THT]
  R1 = Resistor [tolerance=±5% resistance=220 package=THT]
  R2 = Resistor [tolerance=±5% resistance=220 package=THT]
  R3 = Resistor [tolerance=±5% resistance=220 package=THT]
  R4 = Resistor [tolerance=±5% resistance=220 package=THT]
  R5 = Resistor [tolerance=±5% resistance=220 package=THT]
  R6 = Resistor [tolerance=±5% resistance=220 package=THT]
  R7 = Resistor [tolerance=±5% resistance=220 package=THT]
  R8 = Resistor [tolerance=±5% resistance=220 package=THT]

nets:
  N1: Часть1.D8, R8.Pin_0
  N2: Часть1.D9_PWM, R4.Pin_1
  N3: Часть1.GND, DI1.commAnode#7
  N4: Часть1.D2, R7.Pin_1
  N5: Часть1.D3_PWM, R6.Pin_1
  N6: Часть1.D4, R1.Pin_1
  N7: Часть1.D5_PWM, R2.Pin_0
  N8: Часть1.D6_PWM, R3.Pin_0
  N9: Часть1.D7, R5.Pin_0
  N10: DI1.cathodeE, R3.Pin_1
  N11: DI1.cathodeD, R2.Pin_1
  N12: DI1.cathodeC, R4.Pin_0
  N13: DI1.cathodeDP, R1.Pin_0
  N14: DI1.cathodeB, R7.Pin_0
  N15: DI1.cathodeA, R6.Pin_0
  N16: DI1.cathodeF, R5.Pin_1
  N17: DI1.cathodeG, R8.Pin_1
